// Logisim project Alu_16Bit.circ as structural Verilog
module sumarCompleto1Bit (
  input  A,
  input  B,
  input  Cin,
  output R,
  output Cout
);

  wire and_1_out, and_2_out, and_3_out, and_4_out, and_5_out, and_6_out, and_7_out, not_1_out, not_2_out,
       not_3_out, not_4_out, not_5_out, not_6_out;

  not not_1 (not_1_out, A);
  not not_2 (not_2_out, B);
  not not_3 (not_3_out, A);
  not not_4 (not_4_out, Cin);
  not not_5 (not_5_out, B);
  not not_6 (not_6_out, Cin);
  and and_1 (and_1_out, B, Cin);
  and and_2 (and_2_out, A, Cin);
  and and_3 (and_3_out, A, B);
  and and_4 (and_4_out, not_1_out, not_2_out, Cin);
  and and_5 (and_5_out, not_3_out, B, not_4_out);
  and and_6 (and_6_out, A, not_5_out, not_6_out);
  and and_7 (and_7_out, A, B, Cin);
  or or_1 (Cout, and_1_out, and_2_out, and_3_out);
  or or_2 (R, and_4_out, and_5_out, and_6_out, and_7_out);
endmodule

module sumadorCompleto1BitOverflow (
  input  A,
  input  B,
  input  Cin,
  output R,
  output Cout,
  output Overflow
);

  wire and_1_out, and_2_out, and_3_out, and_4_out, and_5_out, and_6_out, and_7_out, and_8_out, and_9_out,
       not_1_out, not_2_out, not_3_out, not_4_out, not_5_out, not_6_out, not_7_out, not_8_out, not_9_out;

  not not_1 (not_1_out, A);
  not not_2 (not_2_out, B);
  not not_3 (not_3_out, A);
  not not_4 (not_4_out, Cin);
  not not_5 (not_5_out, B);
  not not_6 (not_6_out, Cin);
  and and_1 (and_1_out, B, Cin);
  and and_2 (and_2_out, A, Cin);
  and and_3 (and_3_out, A, B);
  not not_7 (not_7_out, A);
  not not_8 (not_8_out, B);
  not not_9 (not_9_out, Cin);
  and and_4 (and_4_out, not_1_out, not_2_out, Cin);
  and and_5 (and_5_out, not_3_out, B, not_4_out);
  and and_6 (and_6_out, A, not_5_out, not_6_out);
  and and_7 (and_7_out, A, B, Cin);
  or or_1 (Cout, and_1_out, and_2_out, and_3_out);
  and and_8 (and_8_out, not_7_out, not_8_out, Cin);
  and and_9 (and_9_out, A, B, not_9_out);
  or or_2 (R, and_4_out, and_5_out, and_6_out, and_7_out);
  or or_3 (Overflow, and_8_out, and_9_out);
endmodule

module AlU_1Bit (
  input  A,
  input  B,
  input  Cin,
  input  [2:0] Operation,
  input  Binvert,
  output Result,
  output Cout
);

  wire and_1_out, multiplexer_1_out, not_1_out, not_2_out, or_1_out, sumarcompleto1bit_1_r;

  not not_1 (not_1_out, B);
  Multiplexer multiplexer_1 (.in0(not_1_out), .in1(B), .out(multiplexer_1_out), .sel(Binvert));  // open: en
  and and_1 (and_1_out, A, multiplexer_1_out);
  or or_1 (or_1_out, A, multiplexer_1_out);
  sumarCompleto1Bit sumarcompleto1bit_1 (
    .A(A), .B(multiplexer_1_out), .Cin(Cin), .R(sumarcompleto1bit_1_r), .Cout(Cout));
  not not_2 (not_2_out, or_1_out);
  Multiplexer #(.select(3), .enable("false")) multiplexer_2 (
    .in1(sumarcompleto1bit_1_r), .in2(and_1_out), .in3(or_1_out), .in5(sumarcompleto1bit_1_r),
    .in7(not_2_out), .out(Result), .sel(Operation));  // open: in0, in4, in6
endmodule

module ALU_16Bits (
  input  Cin,
  input  Binvert,
  input  [15:0] A,
  input  [15:0] B,
  input  [2:0] Operation,
  output Cout
);

  wire alu_1bit_1_cout, alu_1bit_1_result, alu_1bit_2_cout, alu_1bit_3_cout, alu_1bit_4_cout,
       alu_1bit_5_cout, alu_1bit_6_cout, alu_1bit_7_cout, alu_1bit_9_cout, alu_1bit_10_cout,
       alu_1bit_11_cout, alu_1bit_12_cout, alu_1bit_13_cout, alu_1bit_14_cout, alu_1bit_15_cout, Cout8;

  // Probe on A
  AlU_1Bit alu_1bit_1 (
    .Result(alu_1bit_1_result), .A(A[0]), .B(B[0]), .Cin(Cin), .Binvert(Binvert), .Cout(alu_1bit_1_cout),
    .Operation(Operation));
  AlU_1Bit alu_1bit_2 (
    .A(A[1]), .B(B[1]), .Cin(alu_1bit_1_cout), .Binvert(Binvert), .Cout(alu_1bit_2_cout),
    .Operation(Operation));  // open: Result
  AlU_1Bit alu_1bit_3 (
    .A(A[2]), .B(B[2]), .Cin(alu_1bit_2_cout), .Binvert(Binvert), .Cout(alu_1bit_3_cout),
    .Operation(Operation));  // open: Result
  AlU_1Bit alu_1bit_4 (
    .A(A[3]), .B(B[3]), .Cin(alu_1bit_3_cout), .Binvert(Binvert), .Cout(alu_1bit_4_cout),
    .Operation(Operation));  // open: Result
  AlU_1Bit alu_1bit_5 (
    .A(A[4]), .B(B[4]), .Cin(alu_1bit_4_cout), .Binvert(Binvert), .Cout(alu_1bit_5_cout),
    .Operation(Operation));  // open: Result
  AlU_1Bit alu_1bit_6 (
    .A(A[5]), .B(B[5]), .Cin(alu_1bit_5_cout), .Binvert(Binvert), .Cout(alu_1bit_6_cout),
    .Operation(Operation));  // open: Result
  AlU_1Bit alu_1bit_7 (
    .A(A[6]), .B(B[6]), .Cin(alu_1bit_6_cout), .Binvert(Binvert), .Cout(alu_1bit_7_cout),
    .Operation(Operation));  // open: Result
  AlU_1Bit alu_1bit_8 (
    .A(A[7]), .B(B[7]), .Cin(alu_1bit_7_cout), .Binvert(Binvert), .Cout(Cout8), .Operation(Operation));  // open: Result
  AlU_1Bit alu_1bit_9 (
    .A(A[8]), .B(B[8]), .Cin(Cout8), .Binvert(Binvert), .Cout(alu_1bit_9_cout), .Operation(Operation));  // open: Result
  AlU_1Bit alu_1bit_10 (
    .A(A[9]), .B(B[9]), .Cin(alu_1bit_9_cout), .Binvert(Binvert), .Cout(alu_1bit_10_cout),
    .Operation(Operation));  // open: Result
  AlU_1Bit alu_1bit_11 (
    .A(A[10]), .B(B[10]), .Cin(alu_1bit_10_cout), .Binvert(Binvert), .Cout(alu_1bit_11_cout),
    .Operation(Operation));  // open: Result
  AlU_1Bit alu_1bit_12 (
    .A(A[11]), .B(B[11]), .Cin(alu_1bit_11_cout), .Binvert(Binvert), .Cout(alu_1bit_12_cout),
    .Operation(Operation));  // open: Result
  AlU_1Bit alu_1bit_13 (
    .A(A[12]), .B(B[12]), .Cin(alu_1bit_12_cout), .Binvert(Binvert), .Cout(alu_1bit_13_cout),
    .Operation(Operation));  // open: Result
  AlU_1Bit alu_1bit_14 (
    .A(A[13]), .B(B[13]), .Cin(alu_1bit_13_cout), .Binvert(Binvert), .Cout(alu_1bit_14_cout),
    .Operation(Operation));  // open: Result
  AlU_1Bit alu_1bit_15 (
    .A(A[14]), .B(B[14]), .Cin(alu_1bit_14_cout), .Binvert(Binvert), .Cout(alu_1bit_15_cout),
    .Operation(Operation));  // open: Result
  AlU_1Bit alu_1bit_16 (
    .A(A[15]), .B(B[15]), .Cin(alu_1bit_15_cout), .Binvert(Binvert), .Cout(Cout), .Operation(Operation));  // open: Result
  // Probe on B

  // Other names for the same wires on the sheet: Op[2:0] = Operation
endmodule
